// Logisim project animaux_etu.circ as structural Verilog: 6 circuits, main circuit animaux_top
module animaux_top (
  input  quatre_pattes,
  input  ecailles,
  input  ovipare,
  input  ovovivipare,
  output ours,
  output oiseau,
  output ornithorynque,
  output lezard,
  output serpent,
  output indefini
);

  ours_man ours_man_1 (
    .quatre_pattes(quatre_pattes), .ecailles(ecailles), .ovipare(ovipare), .ovovivipare(ovovivipare),
    .ours(ours));
  oiseau_man oiseau_man_1 (
    .quatre_pattes(quatre_pattes), .ecailles(ecailles), .ovipare(ovipare), .ovovivipare(ovovivipare),
    .oiseau(oiseau));
  ornithorynque_auto ornithorynque_auto_1 (
    .quatre_pattes(quatre_pattes), .ecailles(ecailles), .ovipare(ovipare), .ovovivipare(ovovivipare),
    .ornithorynque(ornithorynque));
  lezard_man lezard_man_1 (
    .quatre_pattes(quatre_pattes), .ecailles(ecailles), .ovipare(ovipare), .ovovivipare(ovovivipare),
    .lezard(lezard));
  serpent_auto serpent_auto_1 (
    .quatre_pattes(quatre_pattes), .ecailles(ecailles), .ovipare(ovipare), .ovovivipare(ovovivipare),
    .serpent(serpent));
  nor nor_1 (indefini, ours, oiseau, ornithorynque, lezard, serpent);

  // Notes on the sheet:
  //   Attention, votre version de Logisim
  //   ne contient pas de tracker. Si vous
  //   enregistrez votre projet, toutes les
  //   informations du tracker seront
  //   définitivement effacées.
endmodule

module ours_man (
  input  quatre_pattes,
  input  ecailles,
  input  ovipare,
  input  ovovivipare,
  output ours
);

  wire not_1_out, not_2_out, not_3_out;

  not not_1 (not_1_out, ovipare);
  not not_2 (not_2_out, ovovivipare);
  not not_3 (not_3_out, ecailles);
  and and_1 (ours, quatre_pattes, not_3_out, not_1_out, not_2_out);

  // Notes on the sheet:
  //   Attention, votre version de Logisim
  //   ne contient pas de tracker. Si vous
  //   enregistrez votre projet, toutes les
  //   informations du tracker seront
  //   définitivement effacées.
endmodule

module oiseau_man (
  input  quatre_pattes,
  input  ecailles,
  input  ovipare,
  input  ovovivipare,
  output oiseau
);

  wire not_1_out, not_2_out, not_3_out;

  not not_1 (not_1_out, quatre_pattes);
  not not_2 (not_2_out, ecailles);
  not not_3 (not_3_out, ovovivipare);
  and and_1 (oiseau, not_1_out, not_2_out, ovipare, not_3_out);

  // Notes on the sheet:
  //   Attention, votre version de Logisim
  //   ne contient pas de tracker. Si vous
  //   enregistrez votre projet, toutes les
  //   informations du tracker seront
  //   définitivement effacées.
endmodule

module lezard_man (
  input  quatre_pattes,
  input  ecailles,
  input  ovipare,
  input  ovovivipare,
  output lezard
);

  wire and_1_out, and_2_out, not_1_out, not_2_out;

  not not_1 (not_1_out, ovovivipare);
  not not_2 (not_2_out, ovipare);
  and and_1 (and_1_out, quatre_pattes, ecailles, ovipare, not_1_out);
  and and_2 (and_2_out, quatre_pattes, ecailles, not_2_out, ovovivipare);
  or or_1 (lezard, and_1_out, and_2_out);

  // Notes on the sheet:
  //   Attention, votre version de Logisim
  //   ne contient pas de tracker. Si vous
  //   enregistrez votre projet, toutes les
  //   informations du tracker seront
  //   définitivement effacées.
endmodule

module ornithorynque_auto (
  input  quatre_pattes,
  input  ecailles,
  input  ovipare,
  input  ovovivipare,
  output ornithorynque
);

  wire not_1_out, not_2_out;

  not not_1 (not_1_out, ecailles);
  not not_2 (not_2_out, ovipare);
  and and_1 (ornithorynque, quatre_pattes, not_1_out, not_2_out, ovovivipare);

  // Notes on the sheet:
  //   Attention, votre version de Logisim
  //   ne contient pas de tracker. Si vous
  //   enregistrez votre projet, toutes les
  //   informations du tracker seront
  //   définitivement effacées.
endmodule

module serpent_auto (
  input  quatre_pattes,
  input  ecailles,
  input  ovipare,
  input  ovovivipare,
  output serpent
);

  wire and_1_out, and_2_out, not_1_out, not_2_out, not_3_out;

  not not_1 (not_1_out, quatre_pattes);
  not not_2 (not_2_out, ovipare);
  not not_3 (not_3_out, ovovivipare);
  and and_1 (and_1_out, not_1_out, ecailles, not_2_out, ovovivipare);
  and and_2 (and_2_out, not_1_out, ecailles, ovipare, not_3_out);
  or or_1 (serpent, and_1_out, and_2_out);

  // Notes on the sheet:
  //   Attention, votre version de Logisim
  //   ne contient pas de tracker. Si vous
  //   enregistrez votre projet, toutes les
  //   informations du tracker seront
  //   définitivement effacées.
endmodule
