// Logisim project add_sub_etu.circ as structural Verilog: 6 circuits, main circuit main
module main (
);


  // Notes on the sheet:
  //   Attention, votre version de Logisim
  //   ne contient pas de tracker. Si vous
  //   enregistrez votre projet, toutes les
  //   informations du tracker seront
  //   définitivement effacées.
endmodule

module Add1bit (
  input  a_i,
  input  b_i,
  input  c_i,
  output r_o,
  output c_o
);

  wire and_1_out, and_2_out, and_3_out, xor_1_out;

  xor xor_1 (xor_1_out, a_i, b_i);
  and and_1 (and_1_out, a_i, b_i);
  and and_2 (and_2_out, a_i, c_i);
  and and_3 (and_3_out, b_i, c_i);
  xor xor_2 (r_o, xor_1_out, c_i);
  or or_1 (c_o, and_1_out, and_2_out, and_3_out);

  // Notes on the sheet:
  //   Attention, votre version de Logisim
  //   ne contient pas de tracker. Si vous
  //   enregistrez votre projet, toutes les
  //   informations du tracker seront
  //   définitivement effacées.
endmodule

module Add4bit (
  input  c_i,
  input  [3:0] a_i,
  input  [3:0] b_i,
  output [3:0] r_o,
  output c_out
);

  wire Add1bit_0_c_o, Add1bit_1_c_o, Add1bit_2_c_o;

  Add1bit Add1bit_0 (.a_i(a_i[0]), .b_i(b_i[0]), .c_i(c_i), .r_o(r_o[0]), .c_o(Add1bit_0_c_o));
  Add1bit Add1bit_1 (.a_i(a_i[1]), .b_i(b_i[1]), .c_i(Add1bit_0_c_o), .r_o(r_o[1]), .c_o(Add1bit_1_c_o));
  Add1bit Add1bit_2 (.a_i(a_i[2]), .b_i(b_i[2]), .c_i(Add1bit_1_c_o), .r_o(r_o[2]), .c_o(Add1bit_2_c_o));
  Add1bit Add1bit_3 (.a_i(a_i[3]), .b_i(b_i[3]), .c_i(Add1bit_2_c_o), .r_o(r_o[3]), .c_o(c_out));

  // Notes on the sheet:
  //   Attention, votre version de Logisim
  //   ne contient pas de tracker. Si vous
  //   enregistrez votre projet, toutes les
  //   informations du tracker seront
  //   définitivement effacées.
endmodule

module Sub4bit (
  input  in_1,
  input  [3:0] a_i,
  input  [3:0] b_i,
  output [3:0] r_o,
  output c_o
);

  wire [3:0] not_1_out;

  assign not_1_out = ~b_i;  // NOT_Gate not_1, 4 bits wide
  Add4bit add4bit_1 (.c_i(in_1), .a_i(a_i), .b_i(not_1_out), .r_o(r_o), .c_out(c_o));

  // Notes on the sheet:
  //   Attention, votre version de Logisim
  //   ne contient pas de tracker. Si vous
  //   enregistrez votre projet, toutes les
  //   informations du tracker seront
  //   définitivement effacées.
endmodule

module AddSub4bit (
  input  sel_i,
  input  [3:0] a_i,
  input  [3:0] b_i,
  output [3:0] r_o,
  output c_o,
  output ovf_o
);

  wire [3:0] xor_1_out;

  xor xor_1 (xor_1_out[0], b_i[0], sel_i);
  xor xor_2 (xor_1_out[1], b_i[1], sel_i);
  xor xor_3 (xor_1_out[2], b_i[2], sel_i);
  xor xor_4 (xor_1_out[3], b_i[3], sel_i);
  Add4bit add4bit_1 (.c_i(sel_i), .a_i(a_i), .b_i(xor_1_out), .r_o(r_o), .c_out(c_o));
  xor xor_5 (ovf_o, c_o, sel_i);

  // Notes on the sheet:
  //   Attention, votre version de Logisim
  //   ne contient pas de tracker. Si vous
  //   enregistrez votre projet, toutes les
  //   informations du tracker seront
  //   définitivement effacées.
endmodule

module main_4bits (
  input  sel_i,
  input  [3:0] a_i,
  input  [3:0] b_i,
  output [3:0] r_o,
  output c_o,
  output ovf_o
);


  // Notes on the sheet:
  //   Attention, votre version de Logisim
  //   ne contient pas de tracker. Si vous
  //   enregistrez votre projet, toutes les
  //   informations du tracker seront
  //   définitivement effacées.
endmodule
