// Logisim project LaboTCHINDA.circ as structural Verilog: 3 circuits, main circuit Add1bit
module Add1bit (
  input  a_i,
  input  b_i,
  input  c_i,
  output r_o,
  output c_o
);

  wire and_1_out, and_2_out, and_3_out, xor_1_out;

  xor xor_1 (xor_1_out, a_i, b_i);
  and and_1 (and_1_out, a_i, b_i);
  and and_2 (and_2_out, a_i, c_i);
  and and_3 (and_3_out, b_i, c_i);
  or or_1 (c_o, and_1_out, and_2_out, and_3_out);
  xor xor_2 (r_o, xor_1_out, c_i);

  // Notes on the sheet:
  //   Attention, votre version de Logisim
  //   ne contient pas de tracker. Si vous
  //   enregistrez votre projet, toutes les
  //   informations du tracker seront
  //   définitivement effacées.
endmodule

module Add4bit (
  input  c_i,
  input  [3:0] a_i,
  input  [3:0] b_i,
  output [3:0] r_o,
  output c_o
);

  wire add1bit_0_c_o, add1bit_1_c_o, add1bit_2_c_o;

  Add1bit add1bit_0 (.a_i(a_i[0]), .b_i(b_i[0]), .c_i(c_i), .r_o(r_o[0]), .c_o(add1bit_0_c_o));
  Add1bit add1bit_1 (.a_i(a_i[1]), .b_i(b_i[1]), .c_i(add1bit_0_c_o), .r_o(r_o[1]), .c_o(add1bit_1_c_o));
  Add1bit add1bit_2 (.a_i(a_i[2]), .b_i(b_i[2]), .c_i(add1bit_1_c_o), .r_o(r_o[2]), .c_o(add1bit_2_c_o));
  Add1bit add1bit_3 (.a_i(a_i[3]), .b_i(b_i[3]), .c_i(add1bit_2_c_o), .r_o(r_o[3]), .c_o(c_o));

  // Notes on the sheet:
  //   Attention, votre version de Logisim
  //   ne contient pas de tracker. Si vous
  //   enregistrez votre projet, toutes les
  //   informations du tracker seront
  //   définitivement effacées.
endmodule

module operation (
  input  in_1,
  input  [3:0] Xo,
  output [7:0] out_3
);

  Add4bit add4bit_1 (.c_i(in_1), .a_i(Xo), .b_i(Xo), .r_o(out_3[6:3]), .c_o(out_3[7]));

  assign out_3[2:0] = {Xo[1:0], 1'b0};

  // Notes on the sheet:
  //   Attention, votre version de Logisim
  //   ne contient pas de tracker. Si vous
  //   enregistrez votre projet, toutes les
  //   informations du tracker seront
  //   définitivement effacées.
endmodule
