// Logisim project labo_1_addBits.circ as structural Verilog: 4 circuits, main circuit main
module main (
);

  Add1bit add1bit_1 ();  // open: A, B, C_in, D, c_out

  // Notes on the sheet:
  //   Attention, votre version de Logisim
  //   ne contient pas de tracker. Si vous
  //   enregistrez votre projet, toutes les
  //   informations du tracker seront
  //   définitivement effacées.
endmodule

module Add1bit (
  input  A,
  input  B,
  input  C_in,
  output D,
  output c_out
);

  wire and_1_out, and_2_out, and_3_out, xor_1_out;

  xor xor_1 (xor_1_out, A, B);
  and and_1 (and_1_out, A, B);
  and and_2 (and_2_out, A, C_in);
  and and_3 (and_3_out, B, C_in);
  xor xor_2 (D, xor_1_out, C_in);
  or or_1 (c_out, and_1_out, and_2_out, and_3_out);

  // Notes on the sheet:
  //   Attention, votre version de Logisim
  //   ne contient pas de tracker. Si vous
  //   enregistrez votre projet, toutes les
  //   informations du tracker seront
  //   définitivement effacées.
endmodule

module Add4bits (
  input  C_in,
  input  [3:0] A,
  input  [3:0] B,
  output [3:0] D,
  output C_out
);

  wire Add1bit_0_c_out, Add1bit_1_c_out, Add1bit_2_c_out;

  Add1bit Add1bit_0 (.A(A[0]), .B(B[0]), .C_in(C_in), .D(D[0]), .c_out(Add1bit_0_c_out));
  Add1bit Add1bit_1 (.A(A[1]), .B(B[1]), .C_in(Add1bit_0_c_out), .D(D[1]), .c_out(Add1bit_1_c_out));
  Add1bit Add1bit_2 (.A(A[2]), .B(B[2]), .C_in(Add1bit_1_c_out), .D(D[2]), .c_out(Add1bit_2_c_out));
  Add1bit Add1bit_3 (.A(A[3]), .B(B[3]), .C_in(Add1bit_2_c_out), .D(D[3]), .c_out(C_out));

  // Notes on the sheet:
  //   Attention, votre version de Logisim
  //   ne contient pas de tracker. Si vous
  //   enregistrez votre projet, toutes les
  //   informations du tracker seront
  //   définitivement effacées.
endmodule

module AjoutCompteur (
  output [3:0] D,
  output C_out,
  output [2:0] out_3
);

  wire add4bits_1_c_out, clk_out;
  wire [8:0] counter_1_q;
  wire [8:3] undriven;

  Clock clk (.out(clk_out));
  Clock sysclk ();  // open: out
  Counter #(.width(9), .max('h1ff)) counter_1 (
    .clr(1'b0), .load(1'b0), .up(1'b1), .count(1'b1), .clk(clk_out), .D({undriven, out_3}), .Q(counter_1_q));  // open: carry
  Add4bits add4bits_1 (
    .C_in(counter_1_q[0]), .A(counter_1_q[4:1]), .B(counter_1_q[8:5]), .D(D), .C_out(add4bits_1_c_out));
  // Pins of 3 and 9 bits meet at {undriven, out_3}

  // Notes on the sheet:
  //   Attention, votre version de Logisim
  //   ne contient pas de tracker. Si vous
  //   enregistrez votre projet, toutes les
  //   informations du tracker seront
  //   définitivement effacées.
endmodule
