// Logisim project labo_alu_comp_checksum.circ as structural Verilog: 12 circuits, main circuit Add1bit
module Add1bit (
  input  a_i,
  input  b_i,
  input  c_i,
  output r_o,
  output c_o
);

  wire and_1_out, and_2_out, and_3_out, xor_1_out;

  xor xor_1 (xor_1_out, a_i, b_i);
  and and_1 (and_1_out, a_i, b_i);
  and and_2 (and_2_out, a_i, c_i);
  and and_3 (and_3_out, b_i, c_i);
  xor xor_2 (r_o, xor_1_out, c_i);
  or or_1 (c_o, and_1_out, and_2_out, and_3_out);

  // Notes on the sheet:
  //   Attention, votre version de Logisim
  //   ne contient pas de tracker. Si vous
  //   enregistrez votre projet, toutes les
  //   informations du tracker seront
  //   définitivement effacées.
  //   NE PAS MODIFIER 
endmodule

module Add4bits (
  input  c_i,
  input  [3:0] a_i,
  input  [3:0] b_i,
  output [3:0] r_o,
  output c_o
);

  wire c_1, c_2, c_3;

  Add1bit add1bit_0 (.a_i(a_i[0]), .b_i(b_i[0]), .c_i(c_i), .r_o(r_o[0]), .c_o(c_1));
  Add1bit add1bit_1 (.a_i(a_i[1]), .b_i(b_i[1]), .c_i(c_1), .r_o(r_o[1]), .c_o(c_2));
  Add1bit add1bit_2 (.a_i(a_i[2]), .b_i(b_i[2]), .c_i(c_2), .r_o(r_o[2]), .c_o(c_3));
  Add1bit add1bit_3 (.a_i(a_i[3]), .b_i(b_i[3]), .c_i(c_3), .r_o(r_o[3]), .c_o(c_o));

  // Other names for the same wires on the sheet: a_0 = a_i[0]; a_1 = a_i[1]; a_2 = a_i[2]; a_3 = a_i[3]; b_0 = b_i[0];
  //   b_1 = b_i[1]; b_2 = b_i[2]; b_3 = b_i[3]; c_0 = c_i; c_4 = c_o; r_0 = r_o[0]; r_1 = r_o[1]; r_2 = r_o[2];
  //   r_3 = r_o[3]

  // Notes on the sheet:
  //   Attention, votre version de Logisim
  //   ne contient pas de tracker. Si vous
  //   enregistrez votre projet, toutes les
  //   informations du tracker seront
  //   définitivement effacées.
  //   NE PAS MODIFIER 
endmodule

module AddSub4bits (
  input  sub_nadd_i,
  input  [3:0] a_i,
  input  [3:0] b_i,
  output [3:0] r_o,
  output c_o
);

  wire [3:0] xor_1_out;

  xor xor_1 (xor_1_out[0], sub_nadd_i, b_i[0]);
  xor xor_2 (xor_1_out[1], sub_nadd_i, b_i[1]);
  xor xor_3 (xor_1_out[2], sub_nadd_i, b_i[2]);
  xor xor_4 (xor_1_out[3], sub_nadd_i, b_i[3]);
  Add4bits add4bit_0 (.c_i(sub_nadd_i), .a_i(a_i), .b_i(xor_1_out), .r_o(r_o), .c_o(c_o));

  // Other names for the same wires on the sheet: sub_nadd = sub_nadd_i

  // Notes on the sheet:
  //   Attention, votre version de Logisim
  //   ne contient pas de tracker. Si vous
  //   enregistrez votre projet, toutes les
  //   informations du tracker seront
  //   définitivement effacées.
  //   NE PAS MODIFIER 
endmodule

module Logic (
  input  [3:0] in_1,
  input  [3:0] in_2,
  input  [3:0] in_3,
  output [3:0] out_4
);

  wire [3:0] and_1_out, nand_1_out, or_1_out, xor_1_out;

  assign and_1_out = in_2 & in_3;  // AND_Gate and_1, 4 bits wide
  assign or_1_out = in_2 | in_3;  // OR_Gate or_1, 4 bits wide
  assign nand_1_out = ~(in_2 & in_3);  // NAND_Gate nand_1, 4 bits wide
  assign xor_1_out = in_2 ^ in_3;  // XOR_Gate xor_1, 4 bits wide
  Multiplexer #(.select(2), .width(4), .enable("false")) multiplexer_1 (
    .in0(and_1_out), .in1(or_1_out), .in2(nand_1_out), .in3(xor_1_out), .out(out_4), .sel(in_1[1:0]));

  // Notes on the sheet:
  //   Attention, votre version de Logisim
  //   ne contient pas de tracker. Si vous
  //   enregistrez votre projet, toutes les
  //   informations du tracker seront
  //   définitivement effacées.
  //   A vous de régler le nombre de bits pour l'opcode (supprimez ensuite ce texte)
  //   Vous pouvez aussi renommer l'entrée op_5_2_i si par exemple on veut les bits 5 à 2 
endmodule

module AddSub (
  input  op_i,
  input  [3:0] a_i,
  input  [3:0] b_i,
  output [3:0] r_o,
  output zero_o,
  output negative_o,
  output carry_o,
  output overflow_o
);

  // AND_Gate and_1 is placed but not wired
  AddSub4bits AddSub4bits_0 (.sub_nadd_i(op_i), .a_i(a_i), .b_i(b_i), .r_o({negative_o, r_o[2:0]}), .c_o(carry_o));
  xor xor_1 (overflow_o, carry_o, op_i);
  Comparator #(.width(4)) comparator_1 (.a({negative_o, r_o[2:0]}), .b(4'b0000), .eq(zero_o));  // open: gt, lt

  assign r_o[3] = negative_o;

  // Other names for the same wires on the sheet: carry = carry_o; resultat[3:0] = {negative_o, r_o[2:0]};
  //   sub_nadd = op_i

  // Notes on the sheet:
  //   Attention, votre version de Logisim
  //   ne contient pas de tracker. Si vous
  //   enregistrez votre projet, toutes les
  //   informations du tracker seront
  //   définitivement effacées.
  //   Vous pouvez aussi renommer l'entrée op_5_2_i si par exemple on veut les bits 5 à 2 
  //   A vous de régler le nombre de bits pour l'opcode (supprimez ensuite ce texte)
endmodule

module ALU (
  input  [2:0] op_i,
  input  [3:0] a_i,
  input  [3:0] b_i,
  output [3:0] r_o,
  output negative_o,
  output zero_o,
  output carry_o,
  output overflow_o
);


  // Notes on the sheet:
  //   Attention, votre version de Logisim
  //   ne contient pas de tracker. Si vous
  //   enregistrez votre projet, toutes les
  //   informations du tracker seront
  //   définitivement effacées.
endmodule

module Comp (
  input  [3:0] in_1,
  input  in_2,
  input  in_3,
  input  in_4,
  input  in_5,
  output [3:0] out_6
);

  wire and_1_out, and_2_out, and_3_out, and_4_out, not_1_out, not_2_out, not_3_out, not_4_out, or_1_out,
       or_2_out;

  not not_1 (not_1_out, in_1[2]);
  not not_2 (not_2_out, in_4);
  buf and_1 (and_1_out, not_1_out);  // AND_Gate
  and and_2 (and_2_out, in_1[2], not_2_out);
  and and_3 (and_3_out, not_1_out, not_3_out);
  not not_3 (not_3_out, in_3);
  not not_4 (not_4_out, in_2);
  and and_4 (and_4_out, in_1[2], in_4);
  or or_1 (or_1_out, and_1_out, and_2_out);
  or or_2 (or_2_out, and_3_out, and_4_out);
  Multiplexer #(.select(2), .enable("false")) multiplexer_1 (
    .in0(in_2), .in1(or_2_out), .in2(or_1_out), .in3(not_4_out), .out(out_6[0]), .sel(in_1[1:0]));

  assign out_6[3:1] = 3'b000;

  // Notes on the sheet:
  //   Attention, votre version de Logisim
  //   ne contient pas de tracker. Si vous
  //   enregistrez votre projet, toutes les
  //   informations du tracker seront
  //   définitivement effacées.
endmodule

module CompareHandling (
  input  [3:0] op_i,
  input  z_i,
  input  n_i,
  input  c_i,
  input  v_i,
  output [3:0] cmp_o
);

  wire and_1_out, and_2_out, and_3_out, and_4_out, not_1_out, not_2_out, not_3_out, not_4_out, or_1_out,
       or_2_out;

  not not_1 (not_1_out, op_i[2]);
  not not_2 (not_2_out, c_i);
  buf and_1 (and_1_out, not_1_out);  // AND_Gate
  and and_2 (and_2_out, op_i[2], not_2_out);
  and and_3 (and_3_out, not_1_out, not_3_out);
  not not_3 (not_3_out, n_i);
  not not_4 (not_4_out, z_i);
  and and_4 (and_4_out, op_i[2], c_i);
  or or_1 (or_1_out, and_1_out, and_2_out);
  or or_2 (or_2_out, and_3_out, and_4_out);
  Multiplexer #(.select(2), .enable("false")) multiplexer_1 (
    .in0(z_i), .in1(or_2_out), .in2(or_1_out), .in3(not_4_out), .out(cmp_o[0]), .sel(op_i[1:0]));

  assign cmp_o[3:1] = 3'b000;

  // Notes on the sheet:
  //   Attention, votre version de Logisim
  //   ne contient pas de tracker. Si vous
  //   enregistrez votre projet, toutes les
  //   informations du tracker seront
  //   définitivement effacées.
  //   A vous de régler le nombre de bits pour l'opcode (supprimez ensuite ce texte)
  //   Vous pouvez aussi renommer l'entrée op_5_2_i si par exemple on veut les bits 5 à 2 
endmodule

module CompareError (
  input  [4:0] op_i,
  output err_o
);


  // Notes on the sheet:
  //   Attention, votre version de Logisim
  //   ne contient pas de tracker. Si vous
  //   enregistrez votre projet, toutes les
  //   informations du tracker seront
  //   définitivement effacées.
endmodule

module CompMAXV (
  input  [3:0] a_i,
  input  [3:0] b_i,
  output cmp_o,
  output err_o
);

  wire [4:0] opcode_i_sw5;

  DipSwitch opcode_i (
    .sw1(opcode_i_sw5[4]), .sw2(opcode_i_sw5[3]), .sw3(opcode_i_sw5[2]), .sw4(opcode_i_sw5[1]),
    .sw5(opcode_i_sw5[0]));  // open: sw6, sw7, sw8
  // Comp comp_0: pin names not known; wires that end beside it: opcode_i_sw5, a_i, b_i, cmp_o, err_o

  // Notes on the sheet:
  //   Attention, votre version de Logisim
  //   ne contient pas de tracker. Si vous
  //   enregistrez votre projet, toutes les
  //   informations du tracker seront
  //   définitivement effacées.
  //   NE PAS MODIFIER 
endmodule

module Checksum (
  input  [3:0] a_i,
  input  [3:0] b_i,
  input  [3:0] c_i,
  output [3:0] r_o
);


  // Notes on the sheet:
  //   Attention, votre version de Logisim
  //   ne contient pas de tracker. Si vous
  //   enregistrez votre projet, toutes les
  //   informations du tracker seront
  //   définitivement effacées.
endmodule

module VerifyIntegrity (
  input  [3:0] a_i,
  input  [3:0] b_i,
  input  [3:0] c_i,
  input  [3:0] d_i,
  output valid_o
);


  // Notes on the sheet:
  //   Attention, votre version de Logisim
  //   ne contient pas de tracker. Si vous
  //   enregistrez votre projet, toutes les
  //   informations du tracker seront
  //   définitivement effacées.
endmodule
