// Logisim project labo_alu_etu 13.11.2023.circ as structural Verilog: 7 circuits, main circuit ALU_MAXV
module ALU_MAXV (
  input  [3:0] a_i,
  input  [3:0] b_i,
  output [3:0] c_o,
  output erreur_o
);

  wire [5:0] opcode_i_sw6;

  DipSwitch opcode_i (
    .sw1(opcode_i_sw6[5]), .sw2(opcode_i_sw6[4]), .sw3(opcode_i_sw6[3]), .sw4(opcode_i_sw6[2]),
    .sw5(opcode_i_sw6[1]), .sw6(opcode_i_sw6[0]));  // open: sw7, sw8
  ALU_Top alu_inst (.a_i(a_i), .b_i(b_i), .op_i(opcode_i_sw6), .c_o(c_o), .erreur_o(erreur_o));

  // Notes on the sheet:
  //   Attention, votre version de Logisim
  //   ne contient pas de tracker. Si vous
  //   enregistrez votre projet, toutes les
  //   informations du tracker seront
  //   définitivement effacées.
endmodule

module ALU_Top (
  input  [3:0] a_i,
  input  [3:0] b_i,
  input  [5:0] op_i,
  output [3:0] c_o,
  output erreur_o
);

  wire AddSub_1_carry_o, AddSub_1_negative_o, AddSub_1_zero_o, and_1_out, and_2_out, and_3_out, and_4_out,
       or_1_out, overflow;
  wire [3:0] AddSub_1_r_o, Comp_1_cmp_o, custom_1_s_o, LogicUnit_1_f_o;

  and and_1 (and_1_out, ~op_i[0], ~op_i[1], ~op_i[2], op_i[3], op_i[4], ~op_i[5]);  // AND_Gate
  and and_2 (and_2_out, op_i[0], op_i[1], op_i[2], op_i[3], op_i[4], ~op_i[5]);  // AND_Gate
  and and_3 (and_3_out, ~op_i[3], op_i[4], ~op_i[5]);  // AND_Gate
  AddSub AddSub_1 (
    .a_i(a_i), .b_i(b_i), .op_i(op_i[3:2]), .r_o(AddSub_1_r_o), .overflow_o(overflow),
    .carry_o(AddSub_1_carry_o), .negative_o(AddSub_1_negative_o), .zero_o(AddSub_1_zero_o));
  Comp Comp_1 (
    .carry_i(AddSub_1_carry_o), .negative_i(AddSub_1_negative_o), .zero_i(AddSub_1_zero_o), .a_i(a_i[3]),
    .b_i(b_i[3]), .op_i(op_i[2:0]), .cmp_o(Comp_1_cmp_o));
  LogicUnit LogicUnit_1 (.a_i(a_i), .b_i(b_i), .op_i(op_i[1:0]), .f_o(LogicUnit_1_f_o));
  custom custom_1 (.a_i(a_i), .s_o(custom_1_s_o));
  or or_1 (or_1_out, and_1_out, and_2_out, and_3_out);
  and and_4 (and_4_out, ~op_i[4], overflow, ~op_i[5]);  // AND_Gate
  or or_2 (erreur_o, or_1_out, and_4_out);
  Multiplexer #(.select(2), .width(4), .enable("false")) multiplexer_1 (
    .in0(AddSub_1_r_o), .in1(Comp_1_cmp_o), .in2(LogicUnit_1_f_o), .in3(custom_1_s_o), .out(c_o),
    .sel(op_i[5:4]));

  // Other names for the same wires on the sheet: op_3 = op_i[3]; op_2 = op_i[2]; op_0 = op_i[0]; op_1 = op_i[1];
  //   op_4 = op_i[4]; op_5 = op_i[5]; error = erreur_o

  // Notes on the sheet:
  //   Attention, votre version de Logisim
  //   ne contient pas de tracker. Si vous
  //   enregistrez votre projet, toutes les
  //   informations du tracker seront
  //   définitivement effacées.
endmodule

module AddSub (
  input  [3:0] a_i,
  input  [3:0] b_i,
  input  [1:0] op_i,
  output [3:0] r_o,
  output overflow_o,
  output carry_o,
  output negative_o,
  output zero_o
);

  wire and_1_out, and_2_out, not_1_out, not_2_out, not_3_out, SignedOverflow_1_overflow_o, undriven;

  // AddSub4bit AddSub4bit_1: pin names not known; wires that end beside it: op_i[1], a_i, b_i, r_o
  not not_1 (not_1_out, undriven);
  not not_2 (not_2_out, op_i[1]);
  not not_3 (not_3_out, op_i[0]);
  and and_1 (and_1_out, undriven, not_2_out, op_i[0]);
  and and_2 (and_2_out, not_1_out, op_i[0], op_i[1]);
  SignedOverflow SignedOverflow_1 (
    .a_i(a_i[3]), .b_i(b_i[3]), .r_i(r_o[3]), .s_i(not_3_out), .add_sub_i(op_i[1]),
    .overflow_o(SignedOverflow_1_overflow_o));
  or or_1 (overflow_o, and_1_out, and_2_out, SignedOverflow_1_overflow_o);
  and and_3 (carry_o, undriven, op_i[0]);
  xor xor_1 (negative_o, r_o[3], overflow_o);
  nor nor_1 (zero_o, r_o[0], r_o[1], r_o[2], r_o[3]);

  // Notes on the sheet:
  //   Attention, votre version de Logisim
  //   ne contient pas de tracker. Si vous
  //   enregistrez votre projet, toutes les
  //   informations du tracker seront
  //   définitivement effacées.
endmodule

module Comp (
  input  carry_i,
  input  negative_i,
  input  zero_i,
  input  a_i,
  input  b_i,
  input  [2:0] op_i,
  output [3:0] cmp_o
);

  wire and_1_out, and_2_out, and_3_out, and_4_out, and_5_out, and_6_out, not_1_out, not_2_out, not_3_out,
       not_4_out, not_5_out, not_6_out;

  not not_1 (not_1_out, op_i[1]);
  not not_2 (not_2_out, op_i[2]);
  not not_3 (not_3_out, op_i[0]);
  and and_1 (and_1_out, op_i[0], not_1_out, not_2_out, not_4_out);
  not not_4 (not_4_out, negative_i);
  and and_2 (and_2_out, not_3_out, op_i[1], not_2_out, negative_i);
  and and_3 (and_3_out, op_i[0], op_i[1], not_2_out, not_5_out);
  not not_5 (not_5_out, zero_i);
  and and_4 (and_4_out, not_3_out, not_1_out, op_i[2], zero_i);
  and and_5 (and_5_out, op_i[0], not_1_out, op_i[2], carry_i);
  and and_6 (and_6_out, not_3_out, op_i[1], op_i[2], not_6_out);
  not not_6 (not_6_out, carry_i);
  or or_1 (cmp_o[0], and_1_out, and_2_out, and_3_out, and_4_out, and_5_out, and_6_out);

  assign cmp_o[3:1] = 3'b000;

  // Notes on the sheet:
  //   Attention, votre version de Logisim
  //   ne contient pas de tracker. Si vous
  //   enregistrez votre projet, toutes les
  //   informations du tracker seront
  //   définitivement effacées.
endmodule

module LogicUnit (
  input  [3:0] a_i,
  input  [3:0] b_i,
  input  [1:0] op_i,
  output [3:0] f_o
);

  wire [3:0] and_1_out, nand_1_out, or_1_out, xor_1_out;

  assign and_1_out = a_i & b_i;  // AND_Gate and_1, 4 bits wide
  assign or_1_out = a_i | b_i;  // OR_Gate or_1, 4 bits wide
  assign nand_1_out = ~(a_i & b_i);  // NAND_Gate nand_1, 4 bits wide
  assign xor_1_out = a_i ^ b_i;  // XOR_Gate xor_1, 4 bits wide
  Multiplexer #(.select(2), .width(4), .enable("false")) multiplexer_1 (
    .in0(and_1_out), .in1(or_1_out), .in2(nand_1_out), .in3(xor_1_out), .out(f_o), .sel(op_i));

  // Notes on the sheet:
  //   Attention, votre version de Logisim
  //   ne contient pas de tracker. Si vous
  //   enregistrez votre projet, toutes les
  //   informations du tracker seront
  //   définitivement effacées.
endmodule

module SignedOverflow (
  input  a_i,
  input  b_i,
  input  r_i,
  input  s_i,
  input  add_sub_i,
  output overflow_o
);

  wire and_1_out, and_2_out, and_3_out, and_4_out, not_1_out, not_2_out, not_3_out, not_4_out;

  not not_1 (not_1_out, add_sub_i);
  not not_2 (not_2_out, r_i);
  not not_3 (not_3_out, a_i);
  not not_4 (not_4_out, b_i);
  and and_1 (and_1_out, not_3_out, not_4_out, r_i, s_i, not_1_out);
  and and_2 (and_2_out, a_i, b_i, not_2_out, s_i, not_1_out);
  and and_3 (and_3_out, not_3_out, b_i, r_i, s_i, add_sub_i);
  and and_4 (and_4_out, a_i, not_4_out, not_2_out, s_i, add_sub_i);
  or or_1 (overflow_o, and_1_out, and_2_out, and_3_out, and_4_out);

  // Notes on the sheet:
  //   Attention, votre version de Logisim
  //   ne contient pas de tracker. Si vous
  //   enregistrez votre projet, toutes les
  //   informations du tracker seront
  //   définitivement effacées.
endmodule

module custom (
  input  [3:0] a_i,
  output [3:0] s_o
);

  ExactlyOne xor_1 (.out(s_o[0]), .in0(a_i[0]), .in1(a_i[1]), .in2(a_i[2]), .in3(a_i[3]));

  assign s_o[3:1] = 3'b000;

  // Notes on the sheet:
  //   Attention, votre version de Logisim
  //   ne contient pas de tracker. Si vous
  //   enregistrez votre projet, toutes les
  //   informations du tracker seront
  //   définitivement effacées.
endmodule
