// Logisim project labo_alu_etu(NBKF).circ as structural Verilog: 9 circuits, main circuit ALU_MAXV
module ALU_MAXV (
  input  [3:0] a_i,
  input  [3:0] b_i,
  output [3:0] c_o,
  output erreur_o
);

  wire [5:0] opcode_i_sw6;

  DipSwitch opcode_i (
    .sw1(opcode_i_sw6[5]), .sw2(opcode_i_sw6[4]), .sw3(opcode_i_sw6[3]), .sw4(opcode_i_sw6[2]),
    .sw5(opcode_i_sw6[1]), .sw6(opcode_i_sw6[0]));  // open: sw7, sw8
  ALU_Top alu_inst (.a_i(a_i), .b_i(b_i), .op_i(opcode_i_sw6), .c_o(c_o), .erreur_o(erreur_o));

  // Notes on the sheet:
  //   Attention, votre version de Logisim
  //   ne contient pas de tracker. Si vous
  //   enregistrez votre projet, toutes les
  //   informations du tracker seront
  //   définitivement effacées.
endmodule

module ALU_Top (
  input  [3:0] a_i,
  input  [3:0] b_i,
  input  [5:0] op_i,
  output [3:0] c_o,
  output erreur_o
);

  wire AddSub4bit_1_carry_o, AddSub4bit_1_negative_o, AddSub4bit_1_overflow_o, AddSub4bit_1_zero_o;
  wire [3:0] AddSub4bit_1_r_o, Comparateur_1_c_o, Custom_1_c_o, UniteLogique_1_c_o;

  UniteLogique UniteLogique_1 (.Opcode_i(op_i[3:0]), .a_i(a_i), .b_i(b_i), .c_o(UniteLogique_1_c_o));
  Custom Custom_1 (.a_i(a_i), .c_o(Custom_1_c_o));
  AddSub4bit AddSub4bit_1 (
    .Opcode_i(op_i[3:0]), .a_i(a_i), .b_i(b_i), .zero_o(AddSub4bit_1_zero_o),
    .negative_o(AddSub4bit_1_negative_o), .carry_o(AddSub4bit_1_carry_o), .r_o(AddSub4bit_1_r_o),
    .overflow_o(AddSub4bit_1_overflow_o));
  Comparateur Comparateur_1 (
    .Opcode_i(op_i[3:0]), .zero_i(AddSub4bit_1_zero_o), .negative_i(AddSub4bit_1_negative_o),
    .carry_i(AddSub4bit_1_carry_o), .c_o(Comparateur_1_c_o));
  Opcode Opcode_1 (
    .overflow_i(AddSub4bit_1_overflow_o), .Opcode_i(op_i), .AddSub_r_i(AddSub4bit_1_r_o),
    .Comparateur_r_i(Comparateur_1_c_o), .UniteLogique_r_i(UniteLogique_1_c_o), .Custom_r_i(Custom_1_c_o),
    .c_o(c_o), .error_o(erreur_o));

  // Notes on the sheet:
  //   Attention, votre version de Logisim
  //   ne contient pas de tracker. Si vous
  //   enregistrez votre projet, toutes les
  //   informations du tracker seront
  //   définitivement effacées.
endmodule

module Opcode (
  input  overflow_i,
  input  [5:0] Opcode_i,
  input  [3:0] AddSub_r_i,
  input  [3:0] Comparateur_r_i,
  input  [3:0] UniteLogique_r_i,
  input  [3:0] Custom_r_i,
  output [3:0] c_o,
  output error_o
);

  wire and_1_out, and_2_out, and_3_out, and_4_out, and_5_out, nor_1_out, not_1_out, not_2_out, not_3_out,
       not_4_out, not_5_out, or_1_out;

  Multiplexer #(.select(2), .width(4), .enable("false")) multiplexer_1 (
    .in0(AddSub_r_i), .in1(Comparateur_r_i), .in2(UniteLogique_r_i), .in3(Custom_r_i), .out(c_o),
    .sel(Opcode_i[5:4]));
  nor nor_1 (nor_1_out, Opcode_i[4], Opcode_i[5]);
  not not_1 (not_1_out, Opcode_i[0]);
  not not_2 (not_2_out, Opcode_i[1]);
  not not_3 (not_3_out, Opcode_i[2]);
  and and_1 (and_1_out, Opcode_i[0], Opcode_i[1], Opcode_i[2], Opcode_i[3]);
  not not_4 (not_4_out, Opcode_i[3]);
  not not_5 (not_5_out, Opcode_i[5]);
  and and_2 (and_2_out, not_1_out, not_2_out, not_3_out, Opcode_i[3]);
  and and_3 (and_3_out, Opcode_i[4], not_5_out);
  or or_1 (or_1_out, and_2_out, and_1_out, not_4_out);
  and and_4 (and_4_out, or_1_out, and_3_out);
  and and_5 (and_5_out, overflow_i, nor_1_out);
  or or_2 (error_o, and_5_out, and_4_out);

  // Notes on the sheet:
  //   Attention, votre version de Logisim
  //   ne contient pas de tracker. Si vous
  //   enregistrez votre projet, toutes les
  //   informations du tracker seront
  //   définitivement effacées.
endmodule

module AddSub4bit (
  input  [3:0] Opcode_i,
  input  [3:0] a_i,
  input  [3:0] b_i,
  output zero_o,
  output negative_o,
  output carry_o,
  output [3:0] r_o,
  output overflow_o
);

  wire Add4bit_1_carry0_o, and_1_out, and_2_out, and_3_out, not_1_out, not_2_out, xor_2_out;
  wire [3:0] xor_1_out;

  assign xor_1_out = {4{Opcode_i[3]}} ^ b_i;  // XOR_Gate xor_1, 4 bits wide
  Add4bit Add4bit_1 (
    .c_i(Opcode_i[3]), .a_i(a_i), .b_i(xor_1_out), .r_o(r_o), .carry0_o(Add4bit_1_carry0_o),
    .carry1_o(carry_o));
  not not_1 (not_1_out, Opcode_i[2]);
  not not_2 (not_2_out, Opcode_i[2]);
  xor xor_2 (xor_2_out, carry_o, Add4bit_1_carry0_o);
  nor nor_1 (zero_o, r_o[0], r_o[1], r_o[2], r_o[3]);
  and and_1 (and_1_out, not_1_out, r_o[3]);
  and and_2 (and_2_out, carry_o, Opcode_i[2]);
  and and_3 (and_3_out, not_2_out, xor_2_out);
  or or_1 (overflow_o, and_2_out, and_3_out);
  xor xor_3 (negative_o, and_1_out, and_3_out);

  // Notes on the sheet:
  //   Attention, votre version de Logisim
  //   ne contient pas de tracker. Si vous
  //   enregistrez votre projet, toutes les
  //   informations du tracker seront
  //   définitivement effacées.
endmodule

module Add1bit (
  input  a_i,
  input  b_i,
  input  c_i,
  output r_o,
  output c_o
);

  wire and_1_out, and_2_out, and_3_out, xor_1_out;

  xor xor_1 (xor_1_out, a_i, b_i);
  and and_1 (and_1_out, a_i, b_i);
  and and_2 (and_2_out, a_i, c_i);
  and and_3 (and_3_out, b_i, c_i);
  xor xor_2 (r_o, xor_1_out, c_i);
  or or_1 (c_o, and_1_out, and_2_out, and_3_out);

  // Notes on the sheet:
  //   Attention, votre version de Logisim
  //   ne contient pas de tracker. Si vous
  //   enregistrez votre projet, toutes les
  //   informations du tracker seront
  //   définitivement effacées.
endmodule

module Add4bit (
  input  c_i,
  input  [3:0] a_i,
  input  [3:0] b_i,
  output [3:0] r_o,
  output carry0_o,
  output carry1_o
);

  wire Add1bit_1_c_o, Add1bit_2_c_o;

  Add1bit Add1bit_1 (.a_i(a_i[0]), .b_i(b_i[0]), .c_i(c_i), .r_o(r_o[0]), .c_o(Add1bit_1_c_o));
  Add1bit Add1bit_2 (.a_i(a_i[1]), .b_i(b_i[1]), .c_i(Add1bit_1_c_o), .r_o(r_o[1]), .c_o(Add1bit_2_c_o));
  Add1bit Add1bit_3 (.a_i(a_i[2]), .b_i(b_i[2]), .c_i(Add1bit_2_c_o), .r_o(r_o[2]), .c_o(carry0_o));
  Add1bit Add1bit_4 (.a_i(a_i[3]), .b_i(b_i[3]), .c_i(carry0_o), .r_o(r_o[3]), .c_o(carry1_o));

  // Notes on the sheet:
  //   Attention, votre version de Logisim
  //   ne contient pas de tracker. Si vous
  //   enregistrez votre projet, toutes les
  //   informations du tracker seront
  //   définitivement effacées.
endmodule

module Comparateur (
  input  [3:0] Opcode_i,
  input  zero_i,
  input  negative_i,
  input  carry_i,
  output [3:0] c_o
);

  wire and_1_out, and_2_out, and_3_out, and_4_out, not_1_out, not_2_out, not_3_out, not_4_out, or_1_out,
       or_2_out;

  not not_1 (not_1_out, Opcode_i[2]);
  not not_2 (not_2_out, carry_i);
  and and_1 (and_1_out, negative_i, not_1_out);
  and and_2 (and_2_out, Opcode_i[2], not_2_out);
  not not_3 (not_3_out, negative_i);
  or or_1 (or_1_out, and_1_out, and_2_out);
  and and_3 (and_3_out, not_1_out, not_3_out);
  and and_4 (and_4_out, Opcode_i[2], carry_i);
  not not_4 (not_4_out, zero_i);
  or or_2 (or_2_out, and_3_out, and_4_out);
  Multiplexer #(.select(2), .enable("false")) multiplexer_1 (
    .in0(zero_i), .in1(or_2_out), .in2(or_1_out), .in3(not_4_out), .out(c_o[0]), .sel(Opcode_i[1:0]));

  assign c_o[3:1] = 3'b000;

  // Notes on the sheet:
  //   Attention, votre version de Logisim
  //   ne contient pas de tracker. Si vous
  //   enregistrez votre projet, toutes les
  //   informations du tracker seront
  //   définitivement effacées.
endmodule

module UniteLogique (
  input  [3:0] Opcode_i,
  input  [3:0] a_i,
  input  [3:0] b_i,
  output [3:0] c_o
);

  wire [3:0] and_1_out, nand_1_out, or_1_out, xor_1_out;

  assign and_1_out = a_i & b_i;  // AND_Gate and_1, 4 bits wide
  assign or_1_out = a_i | b_i;  // OR_Gate or_1, 4 bits wide
  assign nand_1_out = ~(a_i & b_i);  // NAND_Gate nand_1, 4 bits wide
  assign xor_1_out = a_i ^ b_i;  // XOR_Gate xor_1, 4 bits wide
  Multiplexer #(.select(2), .width(4), .enable("false")) multiplexer_1 (
    .in0(and_1_out), .in1(or_1_out), .in2(nand_1_out), .in3(xor_1_out), .out(c_o), .sel(Opcode_i[1:0]));

  // Notes on the sheet:
  //   Attention, votre version de Logisim
  //   ne contient pas de tracker. Si vous
  //   enregistrez votre projet, toutes les
  //   informations du tracker seront
  //   définitivement effacées.
endmodule

module Custom (
  input  [3:0] a_i,
  output [3:0] c_o
);

  ExactlyOne xor_1 (.out(c_o[0]), .in0(a_i[0]), .in1(a_i[1]), .in2(a_i[2]), .in3(a_i[3]));

  assign c_o[3:1] = 3'b000;

  // Notes on the sheet:
  //   Attention, votre version de Logisim
  //   ne contient pas de tracker. Si vous
  //   enregistrez votre projet, toutes les
  //   informations du tracker seront
  //   définitivement effacées.
endmodule
