// Logisim project labo_bin_lin.circ as structural Verilog: 6 circuits, main circuit bin_lin_4a16
module main3a8 (
);

  wire en_i_out;
  wire [2:0] bin_i_sw3;
  wire [7:0] bin_lin_lin_o;

  DipSwitch #(.number(3)) bin_i (.sw1(bin_i_sw3[2]), .sw2(bin_i_sw3[1]), .sw3(bin_i_sw3[0]));
  Button en_i (.out(en_i_out));
  bin_lin_3a8 bin_lin (.en_i(en_i_out), .bin_i(bin_i_sw3), .lin_o(bin_lin_lin_o));
  // PortIO #(.number(25)) lin_0: pin names not known; wires that end beside it: {{17{1'b0}}, bin_lin_lin_o}

  // Notes on the sheet:
  //   Attention, votre version de Logisim
  //   ne contient pas de tracker. Si vous
  //   enregistrez votre projet, toutes les
  //   informations du tracker seront
  //   définitivement effacées.
endmodule

module main4a16 (
);

  wire en_i_out;
  wire [3:0] bin_i_sw4;
  wire [15:0] bin_lin_lin_o;

  DipSwitch #(.number(4)) bin_i (.sw1(bin_i_sw4[3]), .sw2(bin_i_sw4[2]), .sw3(bin_i_sw4[1]), .sw4(bin_i_sw4[0]));
  Button en_i (.out(en_i_out));
  bin_lin_4a16 bin_lin (.en_i(en_i_out), .bin_i(bin_i_sw4), .lin_o(bin_lin_lin_o));
  // PortIO #(.number(25)) lin_o: pin names not known; wires that end beside it: {{9{1'b0}}, bin_lin_lin_o}

  // Notes on the sheet:
  //   Attention, votre version de Logisim
  //   ne contient pas de tracker. Si vous
  //   enregistrez votre projet, toutes les
  //   informations du tracker seront
  //   définitivement effacées.
endmodule

module bin_lin_3a8 (
  input  en_i,
  input  [2:0] bin_i,
  output [7:0] lin_o
);

  wire and_1_out, or_1_out, or_2_out, or_3_out, or_4_out;

  or or_1 (or_1_out, bin_i[0], bin_i[1], bin_i[2]);
  or or_2 (or_2_out, bin_i[1], bin_i[2]);
  and and_1 (and_1_out, bin_i[0], bin_i[1]);
  or or_3 (or_3_out, bin_i[0], bin_i[1]);
  and and_2 (lin_o[1], en_i, or_1_out);
  and and_3 (lin_o[2], en_i, or_2_out);
  or or_4 (or_4_out, and_1_out, bin_i[2]);
  and and_4 (lin_o[4], en_i, bin_i[2]);
  and and_5 (lin_o[5], en_i, bin_i[2], or_3_out);
  and and_6 (lin_o[6], en_i, bin_i[2], bin_i[1]);
  and and_7 (lin_o[7], en_i, bin_i[0], bin_i[1], bin_i[2]);
  and and_8 (lin_o[3], en_i, or_4_out);

  assign lin_o[0] = en_i;

  // Notes on the sheet:
  //   Attention, votre version de Logisim
  //   ne contient pas de tracker. Si vous
  //   enregistrez votre projet, toutes les
  //   informations du tracker seront
  //   définitivement effacées.
endmodule

module bin_lin_3a8_sim (
  input  in_1,
  input  [2:0] in_2,
  output [7:0] out_3
);

  Clock sysclk ();  // open: out
  bin_lin_3a8 bin_lin_3a8_1 (.en_i(in_1), .bin_i(in_2), .lin_o(out_3));

  // Notes on the sheet:
  //   Attention, votre version de Logisim
  //   ne contient pas de tracker. Si vous
  //   enregistrez votre projet, toutes les
  //   informations du tracker seront
  //   définitivement effacées.
endmodule

module bin_lin_4a16 (
  input  en_i,
  input  [3:0] bin_i,
  output [15:0] lin_o
);

  wire and_4_out;
  wire [2:0] and_1_out, or_1_out;

  or or_1 (or_1_out[0], bin_i[0], bin_i[3]);
  or or_2 (or_1_out[1], bin_i[1], bin_i[3]);
  or or_3 (or_1_out[2], bin_i[2], bin_i[3]);
  and and_1 (and_1_out[0], bin_i[0], bin_i[3]);
  and and_2 (and_1_out[1], bin_i[1], bin_i[3]);
  and and_3 (and_1_out[2], bin_i[2], bin_i[3]);
  and and_4 (and_4_out, en_i, bin_i[3]);
  bin_lin_3a8 bin_1 (.en_i(en_i), .bin_i(or_1_out), .lin_o(lin_o[7:0]));
  bin_lin_3a8 bin_2 (.en_i(and_4_out), .bin_i(and_1_out), .lin_o(lin_o[15:8]));

  // Notes on the sheet:
  //   Attention, votre version de Logisim
  //   ne contient pas de tracker. Si vous
  //   enregistrez votre projet, toutes les
  //   informations du tracker seront
  //   définitivement effacées.
  //   3 2 1 0
  //   15 14 13 12 11 10 9 8
  //   7 6 5 4 3 2 1 0
endmodule

module bin_lin_4a16_sim (
  input  [3:0] bin_i,
  input  en_i,
  output [15:0] lin_o
);

  Clock sysclk ();  // open: out
  bin_lin_4a16 bin_lin_4a16_1 (.en_i(en_i), .bin_i(bin_i), .lin_o(lin_o));

  // Notes on the sheet:
  //   Attention, votre version de Logisim
  //   ne contient pas de tracker. Si vous
  //   enregistrez votre projet, toutes les
  //   informations du tracker seront
  //   définitivement effacées.
endmodule
