// Logisim project labo_alu_comp_checksum_tchinda_feze_cedrick_vanel.circ as structural Verilog: 14 circuits, main circuit Add1bit
module Add1bit (
  input  a_i,
  input  b_i,
  input  c_i,
  output r_o,
  output c_o
);

  wire and_1_out, and_2_out, and_3_out, xor_1_out;

  xor xor_1 (xor_1_out, a_i, b_i);
  and and_1 (and_1_out, a_i, b_i);
  and and_2 (and_2_out, a_i, c_i);
  and and_3 (and_3_out, b_i, c_i);
  xor xor_2 (r_o, xor_1_out, c_i);
  or or_1 (c_o, and_1_out, and_2_out, and_3_out);

  // Notes on the sheet:
  //   Attention, votre version de Logisim
  //   ne contient pas de tracker. Si vous
  //   enregistrez votre projet, toutes les
  //   informations du tracker seront
  //   définitivement effacées.
  //   NE PAS MODIFIER 
endmodule

module Add4bits (
  input  c_i,
  input  [3:0] a_i,
  input  [3:0] b_i,
  output [3:0] r_o,
  output c_o
);

  wire c_1, c_2, c_3;

  Add1bit add1bit_0 (.a_i(a_i[0]), .b_i(b_i[0]), .c_i(c_i), .r_o(r_o[0]), .c_o(c_1));
  Add1bit add1bit_1 (.a_i(a_i[1]), .b_i(b_i[1]), .c_i(c_1), .r_o(r_o[1]), .c_o(c_2));
  Add1bit add1bit_2 (.a_i(a_i[2]), .b_i(b_i[2]), .c_i(c_2), .r_o(r_o[2]), .c_o(c_3));
  Add1bit add1bit_3 (.a_i(a_i[3]), .b_i(b_i[3]), .c_i(c_3), .r_o(r_o[3]), .c_o(c_o));

  // Other names for the same wires on the sheet: a_0 = a_i[0]; a_1 = a_i[1]; a_2 = a_i[2]; a_3 = a_i[3]; b_0 = b_i[0];
  //   b_1 = b_i[1]; b_2 = b_i[2]; b_3 = b_i[3]; c_0 = c_i; c_4 = c_o; r_0 = r_o[0]; r_1 = r_o[1]; r_2 = r_o[2];
  //   r_3 = r_o[3]

  // Notes on the sheet:
  //   Attention, votre version de Logisim
  //   ne contient pas de tracker. Si vous
  //   enregistrez votre projet, toutes les
  //   informations du tracker seront
  //   définitivement effacées.
  //   NE PAS MODIFIER 
endmodule

module AddSub4bits (
  input  sub_nadd_i,
  input  [3:0] a_i,
  input  [3:0] b_i,
  output [3:0] r_o,
  output c_o
);

  wire [3:0] xor_1_out;

  xor xor_1 (xor_1_out[0], sub_nadd_i, b_i[0]);
  xor xor_2 (xor_1_out[1], sub_nadd_i, b_i[1]);
  xor xor_3 (xor_1_out[2], sub_nadd_i, b_i[2]);
  xor xor_4 (xor_1_out[3], sub_nadd_i, b_i[3]);
  Add4bits add4bit_0 (.c_i(sub_nadd_i), .a_i(a_i), .b_i(xor_1_out), .r_o(r_o), .c_o(c_o));

  // Other names for the same wires on the sheet: sub_nadd = sub_nadd_i

  // Notes on the sheet:
  //   Attention, votre version de Logisim
  //   ne contient pas de tracker. Si vous
  //   enregistrez votre projet, toutes les
  //   informations du tracker seront
  //   définitivement effacées.
  //   NE PAS MODIFIER 
endmodule

module Logic (
  input  [1:0] op_i,
  input  [3:0] a_i,
  input  [3:0] b_i,
  output [3:0] r_o
);

  wire [3:0] and_1_out, nand_1_out, or_1_out, xor_1_out;

  assign or_1_out = a_i | b_i;  // OR_Gate or_1, 4 bits wide
  assign and_1_out = a_i & b_i;  // AND_Gate and_1, 4 bits wide
  assign nand_1_out = ~(a_i & b_i);  // NAND_Gate nand_1, 4 bits wide
  assign xor_1_out = a_i ^ b_i;  // XOR_Gate xor_1, 4 bits wide
  Multiplexer #(.select(2), .width(4), .enable("false")) multiplexer_1 (
    .in0(and_1_out), .in1(or_1_out), .in2(xor_1_out), .in3(nand_1_out), .out(r_o), .sel(op_i));

  // Notes on the sheet:
  //   Attention, votre version de Logisim
  //   ne contient pas de tracker. Si vous
  //   enregistrez votre projet, toutes les
  //   informations du tracker seront
  //   définitivement effacées.
  //   A vous de régler le nombre de bits pour l'opcode (supprimez ensuite ce texte)
  //   Vous pouvez aussi renommer l'entrée op_5_2_i si par exemple on veut les bits 5 à 2 
endmodule

module AddSub (
  input  op_i,
  input  [3:0] a_i,
  input  [3:0] b_i,
  output [3:0] r_o,
  output zero_o,
  output negative_o,
  output carry_o,
  output overflow_o
);

  wire AddSub4bits_0_c_o, and_1_out, and_2_out, and_3_out, and_4_out, not_1_out, not_2_out, not_3_out,
       not_4_out, not_5_out, not_6_out, not_7_out, not_8_out;

  not not_1 (not_1_out, op_i);
  not not_2 (not_2_out, a_i[3]);
  not not_3 (not_3_out, b_i[3]);
  not not_4 (not_4_out, op_i);
  not not_5 (not_5_out, r_o[3]);
  not not_6 (not_6_out, b_i[3]);
  not not_7 (not_7_out, r_o[3]);
  not not_8 (not_8_out, a_i[3]);
  and and_1 (and_1_out, not_1_out, not_2_out, not_3_out, r_o[3]);
  and and_2 (and_2_out, not_4_out, b_i[3], a_i[3], not_5_out);
  and and_3 (and_3_out, op_i, a_i[3], not_6_out, not_7_out);
  and and_4 (and_4_out, op_i, not_8_out, b_i[3], r_o[3]);
  AddSub4bits AddSub4bits_0 (.sub_nadd_i(op_i), .a_i(a_i), .b_i(b_i), .r_o(r_o), .c_o(AddSub4bits_0_c_o));
  or or_1 (overflow_o, and_1_out, and_2_out, and_3_out, and_4_out);
  nor nor_1 (zero_o, r_o[0], r_o[1], r_o[2], r_o[3]);
  xor xor_1 (negative_o, r_o[3], overflow_o);
  xor xor_2 (carry_o, op_i, AddSub4bits_0_c_o);

  // Other names for the same wires on the sheet: a = a_i[3]; b = b_i[3]; op_0 = op_i; overflow = overflow_o;
  //   resultat[3:0] = r_o; signe_r = r_o[3]; zero = zero_o

  // Notes on the sheet:
  //   Attention, votre version de Logisim
  //   ne contient pas de tracker. Si vous
  //   enregistrez votre projet, toutes les
  //   informations du tracker seront
  //   définitivement effacées.
  //   Vous pouvez aussi renommer l'entrée op_5_2_i si par exemple on veut les bits 5 à 2 
  //   A vous de régler le nombre de bits pour l'opcode (supprimez ensuite ce texte)
endmodule

module ALU (
  input  [2:0] op_i,
  input  [3:0] a_i,
  input  [3:0] b_i,
  output [3:0] r_o,
  output negative_o,
  output zero_o,
  output carry_o,
  output overflow_o
);

  wire [3:0] c_out, r_0;

  AddSub AddSub_1 (
    .op_i(op_i[0]), .a_i(a_i), .b_i(b_i), .r_o(r_0), .zero_o(zero_o), .negative_o(negative_o),
    .carry_o(carry_o), .overflow_o(overflow_o));
  Logic Logic_1 (.op_i(op_i[1:0]), .a_i(a_i), .b_i(b_i), .r_o(c_out));
  Multiplexer #(.width(4), .enable("false")) multiplexer_1 (.in0(r_0), .in1(c_out), .out(r_o), .sel(op_i[2]));

  // Other names for the same wires on the sheet: op_addsub = op_i[0]; op_logic[1:0] = op_i[1:0]; op_mux = op_i[2]

  // Notes on the sheet:
  //   Attention, votre version de Logisim
  //   ne contient pas de tracker. Si vous
  //   enregistrez votre projet, toutes les
  //   informations du tracker seront
  //   définitivement effacées.
endmodule

module Comp (
  input  [4:0] op_i,
  input  [3:0] a_i,
  input  [3:0] b_i,
  output cmp_o,
  output err_o
);

  wire ALU_1_carry_o, ALU_1_negative_o, ALU_1_overflow_o, ALU_1_zero_o;

  ALU ALU_1 (
    .op_i(3'b001), .a_i(a_i), .b_i(b_i), .negative_o(ALU_1_negative_o), .zero_o(ALU_1_zero_o),
    .carry_o(ALU_1_carry_o), .overflow_o(ALU_1_overflow_o));  // open: r_o
  CompareError CompareError_1 (.op_i(op_i), .err_o(err_o));
  CompareHandling CompareHandling_1 (
    .op_i({op_i[4:3], op_i[1]}), .n_i(ALU_1_negative_o), .z_i(ALU_1_zero_o), .v_i(ALU_1_overflow_o),
    .c_i(ALU_1_carry_o), .comp_o(cmp_o));

  // Notes on the sheet:
  //   Attention, votre version de Logisim
  //   ne contient pas de tracker. Si vous
  //   enregistrez votre projet, toutes les
  //   informations du tracker seront
  //   définitivement effacées.
endmodule

module CompareHandling (
  input  [2:0] op_i,
  input  n_i,
  input  z_i,
  input  v_i,
  input  c_i,
  output comp_o
);

  wire not_1_out, not_2_out, not_3_out;

  not not_1 (not_1_out, n_i);
  not not_2 (not_2_out, c_i);
  not not_3 (not_3_out, z_i);
  Multiplexer #(.select(3), .enable("false")) multiplexer_1 (
    .in0(not_1_out), .in1(z_i), .in2(n_i), .in3(not_2_out), .in4(not_3_out), .in5(c_i), .in6(1'b1),
    .in7(1'b1), .out(comp_o), .sel(op_i));

  // Notes on the sheet:
  //   Attention, votre version de Logisim
  //   ne contient pas de tracker. Si vous
  //   enregistrez votre projet, toutes les
  //   informations du tracker seront
  //   définitivement effacées.
endmodule

module CompareError (
  input  [4:0] op_i,
  output err_o
);

  wire and_1_out, not_1_out;

  and and_1 (and_1_out, op_i[4], op_i[3]);
  not not_1 (not_1_out, op_i[0]);
  or or_1 (err_o, and_1_out, op_i[2], not_1_out);

  // Notes on the sheet:
  //   Attention, votre version de Logisim
  //   ne contient pas de tracker. Si vous
  //   enregistrez votre projet, toutes les
  //   informations du tracker seront
  //   définitivement effacées.
endmodule

module CompMAXV (
  input  [3:0] a_i,
  input  [3:0] b_i,
  output cmp_o,
  output err_o
);

  wire [4:0] opcode_i_sw5;

  DipSwitch opcode_i (
    .sw1(opcode_i_sw5[4]), .sw2(opcode_i_sw5[3]), .sw3(opcode_i_sw5[2]), .sw4(opcode_i_sw5[1]),
    .sw5(opcode_i_sw5[0]));  // open: sw6, sw7, sw8
  Comp comp_0 (.op_i(opcode_i_sw5), .a_i(a_i), .b_i(b_i), .cmp_o(cmp_o), .err_o(err_o));

  // Notes on the sheet:
  //   Attention, votre version de Logisim
  //   ne contient pas de tracker. Si vous
  //   enregistrez votre projet, toutes les
  //   informations du tracker seront
  //   définitivement effacées.
  //   NE PAS MODIFIER 
endmodule

module Checksum (
  input  [3:0] a_i,
  input  [3:0] b_i,
  input  [3:0] c_i,
  output [3:0] r_o
);

  wire [3:0] alu_1_r_o, alu_2_r_o;

  ALU alu_1 (.op_i(3'b000), .a_i(a_i), .b_i(b_i), .r_o(alu_1_r_o));  // open: negative_o, zero_o, carry_o, overflow_o
  ALU alu_2 (
    .op_i(3'b000), .a_i(alu_1_r_o), .b_i(c_i), .r_o(alu_2_r_o));  // open: negative_o, zero_o, carry_o, overflow_o
  ALU alu_3 (.op_i(3'b001), .b_i(alu_2_r_o), .r_o(r_o));  // open: a_i, negative_o, zero_o, carry_o, overflow_o

  // Notes on the sheet:
  //   Attention, votre version de Logisim
  //   ne contient pas de tracker. Si vous
  //   enregistrez votre projet, toutes les
  //   informations du tracker seront
  //   définitivement effacées.
endmodule

module VerifyIntegrity (
  input  [3:0] a_i,
  input  [3:0] b_i,
  input  [3:0] c_i,
  input  [3:0] d_i,
  output valid_o
);

  wire [3:0] alu_1_r_o, alu_2_r_o, alu_3_r_o;

  ALU alu_1 (.op_i(3'b000), .a_i(a_i), .b_i(b_i), .r_o(alu_1_r_o));  // open: negative_o, zero_o, carry_o, overflow_o
  ALU alu_2 (
    .op_i(3'b000), .a_i(4'b0000), .b_i(d_i), .r_o(alu_2_r_o));  // open: negative_o, zero_o, carry_o, overflow_o
  ALU alu_3 (
    .op_i(3'b000), .a_i(alu_1_r_o), .b_i(c_i), .r_o(alu_3_r_o));  // open: negative_o, zero_o, carry_o, overflow_o
  ALU alu_4 (
    .op_i(3'b001), .a_i(alu_3_r_o), .b_i(alu_2_r_o), .zero_o(valid_o));  // open: r_o, negative_o, carry_o, overflow_o

  // Notes on the sheet:
  //   Attention, votre version de Logisim
  //   ne contient pas de tracker. Si vous
  //   enregistrez votre projet, toutes les
  //   informations du tracker seront
  //   définitivement effacées.
endmodule

module opcode (
  input  overflow_i,
  input  [5:0] opcode_i,
  input  [3:0] addsub_r_i,
  input  [3:0] comparateur_r_i,
  input  [3:0] logic_i,
  input  [3:0] in_6,
  output [3:0] c_o,
  output error_o
);

  wire and_1_out, and_2_out, and_3_out, and_4_out, and_5_out, nor_1_out, not_1_out, not_2_out, not_3_out,
       not_4_out, not_5_out, or_1_out;

  Multiplexer #(.select(2), .width(4), .enable("false")) multiplexer_1 (
    .in0(addsub_r_i), .in1(comparateur_r_i), .in2(logic_i), .in3(in_6), .out(c_o), .sel(opcode_i[5:4]));
  nor nor_1 (nor_1_out, opcode_i[4], opcode_i[5]);
  not not_1 (not_1_out, opcode_i[0]);
  not not_2 (not_2_out, opcode_i[1]);
  not not_3 (not_3_out, opcode_i[2]);
  and and_1 (and_1_out, opcode_i[0], opcode_i[1], opcode_i[2], opcode_i[3]);
  not not_4 (not_4_out, opcode_i[3]);
  not not_5 (not_5_out, opcode_i[5]);
  and and_2 (and_2_out, not_1_out, not_2_out, not_3_out, opcode_i[3]);
  and and_3 (and_3_out, opcode_i[4], not_5_out);
  or or_1 (or_1_out, and_2_out, and_1_out, not_4_out);
  and and_4 (and_4_out, or_1_out, and_3_out);
  and and_5 (and_5_out, overflow_i, nor_1_out);
  or or_2 (error_o, and_5_out, and_4_out);

  // Notes on the sheet:
  //   Attention, votre version de Logisim
  //   ne contient pas de tracker. Si vous
  //   enregistrez votre projet, toutes les
  //   informations du tracker seront
  //   définitivement effacées.
endmodule

module chronogramme (
  output out_1
);

  wire clk_out;
  wire [3:0] counter_1_q, undriven;

  Clock clk (.out(clk_out));
  Counter #(.width(4), .max('hf)) counter_1 (
    .clk(clk_out), .D(undriven), .Q(counter_1_q));  // open: clr, load, up, count, carry
  VerifyIntegrity verifyintegrity_1 (.a_i(4'b1010), .b_i(4'b1011), .c_i(4'b1110), .d_i(counter_1_q), .valid_o(out_1));

  // Notes on the sheet:
  //   Attention, votre version de Logisim
  //   ne contient pas de tracker. Si vous
  //   enregistrez votre projet, toutes les
  //   informations du tracker seront
  //   définitivement effacées.
endmodule
