// Logisim project labo_chenillard_etu.circ as structural Verilog: 6 circuits, main circuit MAXV_CHENILLARD
module MAXV_CHENILLARD (
  input  pulse_load_i,
  input  load_i,
  input  [7:0] switch_i,
  input  clk_i,
  input  nReset_i,
  output [7:0] led_o
);

  wire entree_i_sw7, entree_i_sw8, not_1_out;
  wire [1:0] entree_i_sw2;

  DipSwitch entree_i (
    .sw1(entree_i_sw2[1]), .sw2(entree_i_sw2[0]), .sw7(entree_i_sw7), .sw8(entree_i_sw8));  // open: sw3, sw4, sw5, sw6
  not not_1 (not_1_out, nReset_i);
  chenillard_TOP chenillard_TOP_1 (
    .pulse_Load_i(pulse_load_i), .load_i(load_i), .enable_i(entree_i_sw7), .right_nleft_i(entree_i_sw8),
    .speed_i(entree_i_sw2), .val_i(switch_i), .clk_i(clk_i), .reset_i(not_1_out), .led_o(led_o));

  // Notes on the sheet:
  //   Attention, votre version de Logisim
  //   ne contient pas de tracker. Si vous
  //   enregistrez votre projet, toutes les
  //   informations du tracker seront
  //   définitivement effacées.
endmodule

module chenillard_TOP (
  input  pulse_Load_i,
  input  load_i,
  input  enable_i,
  input  right_nleft_i,
  input  [1:0] speed_i,
  input  [7:0] val_i,
  input  clk_i,
  input  reset_i,
  output [7:0] led_o
);

  wire Bascule_RS_1_q_o, Bascule_RS_2_q_o, demultiplexer_1_out0, demultiplexer_1_out1, or_1_out, or_2_out,
       or_3_out, or_4_out;

  Demultiplexer #(.enable("false")) demultiplexer_1 (
    .out0(demultiplexer_1_out0), .out1(demultiplexer_1_out1), .in(pulse_Load_i), .sel(right_nleft_i));
  or or_1 (or_1_out, led_o[0], reset_i);
  or or_2 (or_2_out, led_o[7], reset_i);
  Bascule_RS Bascule_RS_2 (.S_i(demultiplexer_1_out0), .R_i(or_1_out), .Q_o(Bascule_RS_2_q_o));
  Bascule_RS Bascule_RS_1 (.S_i(demultiplexer_1_out1), .R_i(or_2_out), .Q_o(Bascule_RS_1_q_o));
  or or_3 (or_3_out, Bascule_RS_2_q_o, led_o[7]);
  or or_4 (or_4_out, Bascule_RS_1_q_o, led_o[0]);
  shift_reg_8b shift_reg_8b_1 (
    .ser_l_i(or_3_out), .ser_r_i(or_4_out), .val_o(led_o));  // open: value_load_i, mode_i, clk_i, reset_i

  // Other names for the same wires on the sheet: out_lsb = led_o[0]; out_msb = led_o[7]; rst = reset_i

  // Notes on the sheet:
  //   Attention, votre version de Logisim
  //   ne contient pas de tracker. Si vous
  //   enregistrez votre projet, toutes les
  //   informations du tracker seront
  //   définitivement effacées.
endmodule

module shift_reg_4b (
  input  ser_r_i,
  input  ser_l_i,
  input  [3:0] value_load_i,
  input  [1:0] mode_i,
  input  clk_i,
  input  reset_i,
  output [3:0] val_o
);


  // Notes on the sheet:
  //   Attention, votre version de Logisim
  //   ne contient pas de tracker. Si vous
  //   enregistrez votre projet, toutes les
  //   informations du tracker seront
  //   définitivement effacées.
endmodule

module shift_reg_8b (
  input  ser_l_i,
  input  ser_r_i,
  input  [7:0] value_load_i,
  input  [1:0] mode_i,
  input  clk_i,
  input  reset_i,
  output [7:0] val_o
);


  // Notes on the sheet:
  //   Attention, votre version de Logisim
  //   ne contient pas de tracker. Si vous
  //   enregistrez votre projet, toutes les
  //   informations du tracker seront
  //   définitivement effacées.
endmodule

module timer_28b (
  input  [27:0] value_i,
  input  en_i,
  input  load_i,
  input  clk_i,
  input  reset_i,
  output done_o
);


  // Notes on the sheet:
  //   Attention, votre version de Logisim
  //   ne contient pas de tracker. Si vous
  //   enregistrez votre projet, toutes les
  //   informations du tracker seront
  //   définitivement effacées.
endmodule

module Bascule_RS (
  input  S_i,
  input  R_i,
  output Q_o
);

  wire nor_1_out, nor_2_out;

  nor nor_1 (nor_1_out, S_i, nor_2_out);
  nor nor_2 (nor_2_out, nor_1_out, R_i);
  not not_1 (Q_o, nor_1_out);

  // Notes on the sheet:
  //   Attention, votre version de Logisim
  //   ne contient pas de tracker. Si vous
  //   enregistrez votre projet, toutes les
  //   informations du tracker seront
  //   définitivement effacées.
endmodule
