// Logisim project test_TP5_Note6.circ as structural Verilog: 3 circuits, main circuit main
module main (
  input  ready_i,
  input  color_i1,
  input  color_i0,
  input  RESET,
  output move_o,
  output scan_o,
  output drop_o,
  output dest_init_o,
  output dest_blue_o,
  output dest_red_o,
  output throw_o
);

  wire and_1_out, and_2_out, and_3_out, and_4_out, and_5_out, and_6_out, and_7_out, and_8_out, and_9_out,
       and_10_out, and_12_out, Clk, CNT, or_1_out, Q6;
  wire [6:0] or_7_out;

  Clock u_clk (.out(Clk));
  or or_1 (or_1_out, dest_blue_o, dest_red_o, dest_init_o);
  Clock sysclk ();  // open: out
  Counter #(.width(2), .max('h2)) counter_1 (
    .clr(1'b0), .load(1'b0), .up(1'b0), .count(or_1_out), .clk(Clk), .carry(CNT));  // open: D, Q
  and and_1 (and_1_out, dest_init_o, CNT);
  and and_2 (and_2_out, Q6, ready_i);
  and and_3 (and_3_out, scan_o, color_i1, color_i0);
  and and_4 (and_4_out, ~ready_i, Q6);  // AND_Gate
  or or_2 (or_7_out[5], and_2_out, and_3_out);
  and and_5 (and_5_out, scan_o, color_i1, ~color_i0);  // AND_Gate
  and and_6 (and_6_out, dest_blue_o, ~CNT);  // AND_Gate
  and and_7 (and_7_out, scan_o, ~color_i1, color_i0);  // AND_Gate
  and and_8 (and_8_out, dest_red_o, ~CNT);  // AND_Gate
  and and_9 (and_9_out, dest_blue_o, CNT);
  and and_10 (and_10_out, dest_red_o, CNT);
  and and_11 (or_7_out[1], scan_o, ~color_i1, ~color_i0);  // AND_Gate
  and and_12 (and_12_out, dest_init_o, ~CNT);  // AND_Gate
  or or_3 (or_7_out[6], and_4_out, and_1_out, throw_o);
  or or_4 (or_7_out[4], and_5_out, and_6_out);
  or or_5 (or_7_out[3], and_7_out, and_8_out);
  or or_6 (or_7_out[2], and_9_out, and_10_out);
  or or_7 (or_7_out[0], and_12_out, drop_o);
  memory memory_1 (
    .in_1(or_7_out), .clk(Clk), .reset(RESET),
    .out_4({Q6, scan_o, dest_blue_o, dest_red_o, drop_o, throw_o, dest_init_o}));
  or or_8 (move_o, dest_blue_o, dest_init_o, dest_red_o);

  // Other names for the same wires on the sheet: Q0 = dest_init_o; Q1 = throw_o; Q2 = drop_o; Q3 = dest_red_o;
  //   Q4 = dest_blue_o; Q5 = scan_o; C0 = color_i0; C1 = color_i1; R = ready_i

  // Notes on the sheet:
  //   Attention, votre version de Logisim
  //   ne contient pas de tracker. Si vous
  //   enregistrez votre projet, toutes les
  //   informations du tracker seront
  //   définitivement effacées.
endmodule

module compteur (
  input  Clk,
  input  En,
  output o
);

  wire [1:0] adder_1_out, CPT, multiplexer_1_out, multiplexer_2_out;

  Adder #(.width(2)) adder_1 (.a(CPT), .b(2'b01), .out(adder_1_out));  // open: cin, cout
  Multiplexer #(.width(2), .enable("false")) multiplexer_1 (
    .in0(CPT), .in1(adder_1_out), .out(multiplexer_1_out), .sel(En));
  Multiplexer #(.width(2), .enable("false")) multiplexer_2 (
    .in0(multiplexer_1_out), .in1(2'b00), .out(multiplexer_2_out), .sel(o));
  Register #(.width(2)) register_1 (.D(multiplexer_2_out), .en(1'b1), .clk(Clk), .Q(CPT));  // open: clr
  Comparator #(.width(2)) comparator_1 (.a(CPT), .b(2'b10), .eq(o));  // open: gt, lt

  // Notes on the sheet:
  //   Attention, votre version de Logisim
  //   ne contient pas de tracker. Si vous
  //   enregistrez votre projet, toutes les
  //   informations du tracker seront
  //   définitivement effacées.
endmodule

module memory (
  input  [6:0] in_1,
  input  clk,
  input  reset,
  output [6:0] out_4
);

  D_Flip_Flop d_ff_1 (.D(in_1[6]), .clk(clk), .Q(out_4[6]), .preset(reset));  // open: Qn, reset
  Register #(.width(6)) register_1 (.D(in_1[5:0]), .en(1'b1), .clk(clk), .Q(out_4[5:0]), .clr(reset));

  // Notes on the sheet:
  //   Attention, votre version de Logisim
  //   ne contient pas de tracker. Si vous
  //   enregistrez votre projet, toutes les
  //   informations du tracker seront
  //   définitivement effacées.
endmodule
