// Logisim project processeur_ARO2.circ as structural Verilog: 4 circuits, main circuit main
module main (
);

  wire clk, RESET_out, sysclk;
  wire [7:0] instr_mem_8b_1_instr_o;
  wire [15:0] instr_mem_16b_1_instr_o, processeur_aro2_1_instr_addr_o;

  Button RESET (.out(RESET_out));
  Clock #(.highDuration(4), .lowDuration(4)) u_clk (.out(clk));
  Clock u_sysclk (.out(sysclk));
  // Probe on processeur_aro2_1_instr_addr_o
  processeur_ARO2 processeur_aro2_1 (
    .instr_data_i({16{1'b0}}), .memory_rd_data_i({16{1'b0}}), .rst_i(RESET_out), .clk_i(clk),
    .instr_addr_o(processeur_aro2_1_instr_addr_o));  // open: memory_addr_o, memory_wr_data_o, memory_str_data_o, memory_ldr_data, memory_high_byte_o, memory_low_byte_o
  // Probe on processeur_aro2_1_instr_addr_o[15:1]
  Instr_mem_8b instr_mem_8b_1 (.addr_i(processeur_aro2_1_instr_addr_o[15:1]), .instr_o(instr_mem_8b_1_instr_o));
  instr_mem_16b instr_mem_16b_1 (.addr_i(processeur_aro2_1_instr_addr_o[15:1]), .instr_o(instr_mem_16b_1_instr_o));
  // Probe on instr_mem_8b_1_instr_o
  // Probe on instr_mem_16b_1_instr_o

  // Notes on the sheet:
  //   Attention, votre version de Logisim
  //   ne contient pas de tracker. Si vous
  //   enregistrez votre projet, toutes les
  //   informations du tracker seront
  //   définitivement effacées.
  //   Adresse avec la vision
  //   depuis le processeur
  //   Adresse avec la vision
  //   depuis la memoire
endmodule

module processeur_ARO2 (
  input  [15:0] instr_data_i,
  input  [15:0] memory_rd_data_i,
  input  rst_i,
  input  clk_i,
  output [15:0] instr_addr_o,
  output [14:0] memory_addr_o,
  output [15:0] memory_wr_data_o,
  output memory_str_data_o,
  output memory_ldr_data,
  output memory_high_byte_o,
  output memory_low_byte_o
);

  wire [15:0] adder_1_out;

  // Probe on adder_1_out
  Adder #(.width(16)) adder_1 (.a(instr_addr_o), .b(16'h2), .out(adder_1_out), .cin(1'b0));  // open: cout
  Register #(.width(16)) PC (.D(adder_1_out), .en(1'b1), .clk(clk_i), .Q(instr_addr_o), .clr(rst_i));
  // Probe on instr_addr_o

  assign memory_addr_o = {15{1'b0}};
  assign memory_high_byte_o = 1'b0;
  assign memory_ldr_data = 1'b0;
  assign memory_low_byte_o = 1'b0;
  assign memory_str_data_o = 1'b0;
  assign memory_wr_data_o = {16{1'b0}};

  // Other names for the same wires on the sheet: clk_s = clk_i; instr_addr_s[15:0] = instr_addr_o;
  //   instr_data_s[15:0] = instr_data_i; memory_rd_data_s[15:0] = memory_rd_data_i; rst_s = rst_i

  // Notes on the sheet:
  //   Attention, votre version de Logisim
  //   ne contient pas de tracker. Si vous
  //   enregistrez votre projet, toutes les
  //   informations du tracker seront
  //   définitivement effacées.
  //   Intruction memory inputs
  //   Memory interface inputs
  //   Standard inputs
  //   Processeur simplifié pour le cours ARO2
  //   Incrément du PC
  //   Instruction memory outputs
  //   Memory interface outputs
endmodule

module Instr_mem_8b (
  input  [14:0] addr_i,
  output [7:0] instr_o
);

  ROM #(.addrWidth(15)) rom_1 (.addr(addr_i), .data(instr_o));

  // Notes on the sheet:
  //   Attention, votre version de Logisim
  //   ne contient pas de tracker. Si vous
  //   enregistrez votre projet, toutes les
  //   informations du tracker seront
  //   définitivement effacées.
  //   contents of rom_1 (hex, n*v repeats v):
  //   1 2 3 4 5 6 7 8 a
endmodule

module instr_mem_16b (
  input  [14:0] addr_i,
  output [15:0] instr_o
);

  ROM #(.addrWidth(15), .dataWidth(16)) rom_1 (.addr(addr_i), .data(instr_o));

  // Notes on the sheet:
  //   Attention, votre version de Logisim
  //   ne contient pas de tracker. Si vous
  //   enregistrez votre projet, toutes les
  //   informations du tracker seront
  //   définitivement effacées.
  //   contents of rom_1 (hex, n*v repeats v):
  //   2001 2102 2203 2304 2405 2506 2607 2708 180a
endmodule
